# Fritzing sketch Circuit (saved by Fritzing 0.9.3b)
breadboards: 1

parts:
  R1 = Resistor [tolerance=±5% resistance=10k package=THT]
  Part1 = Photon
  Q1 = Basic FET N-Channel [package="TO220 [THT]"]
  Q2 = Basic FET N-Channel [package="TO220 [THT]"]
  R2 = Resistor [tolerance=±5% resistance=10k package=THT]
  Q3 = Basic FET N-Channel [package="TO220 [THT]"]
  R3 = Resistor [tolerance=±5% resistance=10k package=THT]
  LED2 = Super Flux RGB LED (com. anode)

nets:
  N1: R1.Pin_0, Part1.GND, Part1.D2, Q1.source, Q2.source, R2.Pin_0, Q3.source, R3.Pin_0
  N2: R1.Pin_1, Part1.D0, Q1.gate
  N3: Part1.VIN, LED2.common_anode
  N4: Part1.D1, Q2.gate, R2.Pin_1
  N5: Q1.drain, LED2.red_cathode
  N6: Q2.drain, LED2.green_cathode
  N7: Q3.gate, R3.Pin_1
  N8: Q3.drain, LED2.blue_cathode

notes:
  MOSFET DRAIN = LED CATHODE
  MOSFET SOURCE = GROUND
  MOSFET GATE = ARDUINO 0-5V, PULL DOWN
  RGB LED STRIPS
  COMMON ANODE
